// Logisim project AryaBhata_Processor5.circ as structural Verilog: 12 circuits, main circuit CPU_Compilation
module Instrucion_decode_logic (
  input  [15:0] IR_data,
  input  CONTROL,
  input  CLOCK_I,
  input  DCDR_EN_1,
  input  CLEAR,
  input  INR_SC,
  input  DCDR_EN_2,
  input  CLOCK_SC,
  output I,
  output D0,
  output D1,
  output D2,
  output D3,
  output D4,
  output D5,
  output D6,
  output D7,
  output T7,
  output T6,
  output T5,
  output T4,
  output T3,
  output T2,
  output T1,
  output T0,
  output r,
  output rB0,
  output rB1,
  output rB2,
  output rB3,
  output rB4,
  output rB5,
  output rB6,
  output rB7,
  output rB8,
  output rB9,
  output rB10,
  output rB11
);

  wire multiplexer_1_out, not_1_out;
  wire [15:8] sequence_counter_1_t0_to_t15;

  Multiplexer multiplexer_1 (.in0(I), .in1(IR_data[15]), .out(multiplexer_1_out), .sel(CONTROL));
  D_Flip_Flop d_ff_1 (.D(multiplexer_1_out), .clk(CLOCK_I), .Q(I));  // open: Qn, preset, reset
  not not_1 (not_1_out, I);
  and and_1 (r, D7, not_1_out, T3);
  Sequence_Counter sequence_counter_1 (
    .CLEAR(CLEAR), .INR_SC(INR_SC), .DCDR_EN(DCDR_EN_2), .CLOCK(CLOCK_SC),
    .T0_to_T15({sequence_counter_1_t0_to_t15, T7, T6, T5, T4, T3, T2, T1, T0}));
  and and_2 (rB0, r, IR_data[0]);
  and and_3 (rB1, r, IR_data[1]);
  and and_4 (rB2, r, IR_data[2]);
  and and_5 (rB3, r, IR_data[3]);
  and and_6 (rB4, r, IR_data[4]);
  and and_7 (rB5, r, IR_data[5]);
  and and_8 (rB6, r, IR_data[6]);
  and and_9 (rB7, r, IR_data[7]);
  and and_10 (rB8, r, IR_data[8]);
  and and_11 (rB9, r, IR_data[9]);
  and and_12 (rB10, r, IR_data[10]);
  and and_13 (rB11, r, IR_data[11]);
  Decoder #(.select(3)) decoder_1 (
    .out0(D0), .out1(D1), .out2(D2), .out3(D3), .out4(D4), .out5(D5), .out6(D6), .out7(D7),
    .sel(IR_data[14:12]), .en(DCDR_EN_1));

  // Other names for the same wires on the sheet: B0 = IR_data[0]; B1 = IR_data[1]; B2 = IR_data[2]; B3 = IR_data[3];
  //   B4 = IR_data[4]; B5 = IR_data[5]; B6 = IR_data[6]; B7 = IR_data[7]; B8 = IR_data[8]; B9 = IR_data[9];
  //   B10 = IR_data[10]; B11 = IR_data[11]
endmodule

module Sequence_Counter (
  input  CLEAR,
  input  INR_SC,
  input  DCDR_EN,
  input  CLOCK,
  output [15:0] T0_to_T15
);

  wire [3:0] adder_1_out, multiplexer_1_out, register_1_q;

  Adder #(.width(4)) adder_1 (.a(register_1_q), .b(4'b0001), .out(adder_1_out));  // open: cin, cout
  Multiplexer #(.select(2), .width(4)) multiplexer_1 (
    .in0(register_1_q), .in1(adder_1_out), .in2(4'b0000), .in3(4'b0000), .out(multiplexer_1_out),
    .sel({CLEAR, INR_SC}));
  Register #(.width(4)) register_1 (.D(multiplexer_1_out), .clk(CLOCK), .Q(register_1_q));  // open: en, clr
  Decoder #(.select(4)) decoder_1 (
    .out0(T0_to_T15[0]), .out1(T0_to_T15[1]), .out2(T0_to_T15[2]), .out3(T0_to_T15[3]), .out4(T0_to_T15[4]),
    .out5(T0_to_T15[5]), .out6(T0_to_T15[6]), .out7(T0_to_T15[7]), .out8(T0_to_T15[8]), .out9(T0_to_T15[9]),
    .out10(T0_to_T15[10]), .out11(T0_to_T15[11]), .out12(T0_to_T15[12]), .out13(T0_to_T15[13]),
    .out14(T0_to_T15[14]), .out15(T0_to_T15[15]), .sel(register_1_q), .en(DCDR_EN));
endmodule

module instructionRegister (
  input  [15:0] DATA_IN,
  input  LOAD,
  input  CLOCK,
  output [15:0] DATA_OUT
);

  wire [15:0] multiplexer_1_out;

  Multiplexer #(.width(16)) multiplexer_1 (.in0(DATA_OUT), .in1(DATA_IN), .out(multiplexer_1_out), .sel(LOAD));
  Register #(.width(16)) register_1 (.D(multiplexer_1_out), .clk(CLOCK), .Q(DATA_OUT));  // open: en, clr
endmodule

module commonRegAcDrTr (
  input  INR,
  input  CLEAR,
  input  CLOCK,
  input  [15:0] DATA_IN,
  input  LOAD,
  output [15:0] DATA_OUT
);

  wire [15:0] adder_1_out, multiplexer_1_out, multiplexer_2_out, multiplexer_3_out;

  Adder #(.width(16)) adder_1 (.a(DATA_OUT), .b(16'h1), .out(adder_1_out));  // open: cin, cout
  Multiplexer #(.width(16)) multiplexer_1 (.in0(DATA_OUT), .in1(adder_1_out), .out(multiplexer_1_out), .sel(INR));
  Multiplexer #(.width(16)) multiplexer_2 (.in0(multiplexer_1_out), .in1(DATA_IN), .out(multiplexer_2_out), .sel(LOAD));
  Multiplexer #(.width(16)) multiplexer_3 (
    .in0(multiplexer_2_out), .in1({16{1'b0}}), .out(multiplexer_3_out), .sel(CLEAR));
  Register #(.width(16)) register_1 (.D(multiplexer_3_out), .clk(CLOCK), .Q(DATA_OUT));  // open: en, clr
endmodule

module programCounterReg (
  input  INR,
  input  CLEAR,
  input  CLOCK,
  input  LOAD,
  input  [15:0] DATA_IN,
  output [15:0] DATA_OUT
);

  wire [11:0] adder_1_out, multiplexer_1_out, multiplexer_2_out, multiplexer_3_out;

  Adder #(.width(12)) adder_1 (.a(DATA_OUT[11:0]), .b(12'h1), .out(adder_1_out));  // open: cin, cout
  Multiplexer #(.width(12)) multiplexer_1 (.in0(DATA_OUT[11:0]), .in1(adder_1_out), .out(multiplexer_1_out), .sel(INR));
  Multiplexer #(.width(12)) multiplexer_2 (
    .in0(multiplexer_1_out), .in1(DATA_IN[11:0]), .out(multiplexer_2_out), .sel(LOAD));
  Multiplexer #(.width(12)) multiplexer_3 (
    .in0(multiplexer_2_out), .in1({12{1'b0}}), .out(multiplexer_3_out), .sel(CLEAR));
  Register #(.width(12)) register_1 (.D(multiplexer_3_out), .clk(CLOCK), .Q(DATA_OUT[11:0]));  // open: en, clr

  assign DATA_OUT[15:12] = 4'b0000;
endmodule

module addressRegister (
  input  INR,
  input  CLEAR,
  input  CLOCK,
  input  LOAD,
  input  [15:0] DATA_IN,
  output [11:0] AddressPin,
  output [15:0] DATA_OUT
);

  wire [11:0] adder_1_out, multiplexer_1_out, multiplexer_2_out, multiplexer_3_out;

  Adder #(.width(12)) adder_1 (.a(AddressPin), .b(12'h1), .out(adder_1_out));  // open: cin, cout
  Multiplexer #(.width(12)) multiplexer_1 (.in0(AddressPin), .in1(adder_1_out), .out(multiplexer_1_out), .sel(INR));
  Multiplexer #(.width(12)) multiplexer_2 (
    .in0(multiplexer_1_out), .in1(DATA_IN[11:0]), .out(multiplexer_2_out), .sel(LOAD));
  Multiplexer #(.width(12)) multiplexer_3 (
    .in0(multiplexer_2_out), .in1({12{1'b0}}), .out(multiplexer_3_out), .sel(CLEAR));
  Register #(.width(12)) register_1 (.D(multiplexer_3_out), .clk(CLOCK), .Q(AddressPin));  // open: en, clr

  assign DATA_OUT = {4'b0000, AddressPin};
endmodule

module CPU_Compilation (
  input  [15:0] in_1,
  input  [15:0] in_2,
  input  RST,
  input  in_4
);

  wire AC_EQUAL_0, AC_LOAD, ADD_OUTPUT, and_6_out, and_7_out, and_8_out, and_9_out, and_10_out, and_13_out,
       and_14_out, and_15_out, and_16_out, and_17_out, AND_OUTPUT, AR_INR_n, AR_LOAD, BSA, BUN, CLEAR_SC,
       CLK, D0, D1, D2, D3, D4, D5, D6, D7, d7_IT3, DR, DR_EQUAL_0, I, INR_SC, ISZ, mem_acc_by_mem_ref,
       not_1_out, not_2_out, not_3_out, or_7_out, or_11_out, PC_INR, PC_LOAD_X1, r, rB0, rB1, rB2, rB3, rB4,
       rB5, rB6, rB7, rB8, rB9, rB10, rB11, Read_en, STA, T0, T1, T2, T3, T4, T5, T6, T7, Write_en, X2, X3,
       X4, X5, X6, X7;
  wire [2:0] ALU_SELECT_LINE, BUS_SELECT_LINE;
  wire [15:0] AC_DATA, data_path_1_ir_data, DR_DATA;

  Clock u_CLK (.out(CLK));
  not not_1 (not_1_out, D7);
  and and_1 (d7_IT3, not_1_out, I, T3);
  and and_2 (ISZ, T6, D6);
  not not_2 (not_2_out, rB0);
  and and_3 (AR_INR_n, D5, T4);
  and and_4 (DR, T5, D2);
  and and_5 (STA, T4, D3);
  buf or_1 (X5, T2);  // OR_Gate
  and and_6 (and_6_out, not_2_out, INR_SC);
  or or_2 (AR_LOAD, T0, T2, d7_IT3);
  or or_3 (X3, DR, ISZ);
  buf or_4 (X4, STA);  // OR_Gate
  or or_5 (X7, T1, d7_IT3, mem_acc_by_mem_ref);
  and and_7 (and_7_out, D0, T4);
  and and_8 (and_8_out, D1, T4);
  and and_9 (and_9_out, D2, T4);
  and and_10 (and_10_out, D6, T4);
  Instrucion_decode_logic instrucion_decode_logic_1 (
    .IR_data(data_path_1_ir_data), .CONTROL(T2), .CLOCK_I(CLK), .DCDR_EN_1(1'b1), .CLEAR(CLEAR_SC),
    .INR_SC(INR_SC), .DCDR_EN_2(1'b1), .CLOCK_SC(CLK), .I(I), .D0(D0), .D1(D1), .D2(D2), .D3(D3), .D4(D4),
    .D5(D5), .D6(D6), .D7(D7), .T7(T7), .T6(T6), .T5(T5), .T4(T4), .T3(T3), .T2(T2), .T1(T1), .T0(T0), .r(r),
    .rB0(rB0), .rB1(rB1), .rB2(rB2), .rB3(rB3), .rB4(rB4), .rB5(rB5), .rB6(rB6), .rB7(rB7), .rB8(rB8),
    .rB9(rB9), .rB10(rB10), .rB11(rB11));
  or or_6 (X2, T0, AR_INR_n);
  ALU_SELECT_GENERATOR alu_select_generator_1 (
    .a1(AND_OUTPUT), .a3(DR), .a5(rB9), .a7(rB6), .a2(ADD_OUTPUT), .a6(rB7), .n2n1n0(ALU_SELECT_LINE));  // open: a4
  or or_7 (or_7_out, in_4, and_6_out);
  or or_8 (Read_en, T1, d7_IT3, and_7_out, and_8_out, and_9_out, and_10_out);
  D_Flip_Flop d_ff_1 (.D(or_7_out), .clk(CLK), .Q(INR_SC));  // open: Qn, preset, reset
  or or_9 (mem_acc_by_mem_ref, and_7_out, and_8_out, and_9_out, and_10_out);
  not not_3 (not_3_out, AC_DATA[15]);
  and and_11 (BUN, T4, D4);
  and and_12 (BSA, T5, D5);
  and and_13 (and_13_out, D6, T5);
  and and_14 (and_14_out, rB4, not_3_out);
  and and_15 (and_15_out, rB3, AC_DATA[15]);
  and and_16 (and_16_out, rB2, AC_EQUAL_0);
  and and_17 (and_17_out, ISZ, DR_EQUAL_0);
  or or_10 (PC_LOAD_X1, BUN, BSA);
  or or_11 (or_11_out, ADD_OUTPUT, rB7, rB6);
  or or_12 (PC_INR, T1, and_14_out, and_15_out, and_16_out, and_17_out);
  BUS_SELECT_GENERATOR bus_select_generator_1 (
    .x1(PC_LOAD_X1), .x2(X2), .x3(X3), .x4(X4), .x5(X5), .x6(X6), .x7(X7), .o3o2o1(BUS_SELECT_LINE));
  or or_13 (Write_en, STA, ISZ, AR_INR_n);
  and and_18 (ADD_OUTPUT, D1, T5);
  and and_19 (AND_OUTPUT, D0, T5);
  Data_Path data_path_1 (
    .Write_en_memory(Write_en), .Read_en_memory(Read_en), .CLOCK(CLK), .AR_INR(AR_INR_n), .AR_LD(AR_LOAD),
    .PC_INR(PC_INR), .PC_CLR(RST), .PC_LD(PC_LOAD_X1), .S2S1S0(BUS_SELECT_LINE), .DR_INR(and_13_out),
    .DR_LD(mem_acc_by_mem_ref), .AC_INR(rB5), .AC_CLR(rB11), .AC_LD(AC_LOAD), .IR_LD(T1),
    .ALU_SELECT(ALU_SELECT_LINE), .compE(rB8), .D1T5(ADD_OUTPUT), .Eclear(rB10), .rB7(rB7),
    .Eload(or_11_out), .rB6(rB6), .DR_DATA(DR_DATA), .AC_DATA(AC_DATA), .IR_DATA(data_path_1_ir_data));  // open: AR_CLR, DR_CLR, TR_INR, TR_CLR, TR_LD
  Comparator #(.width(16)) comparator_1 (.a(in_1), .b(AC_DATA), .eq(AC_EQUAL_0));  // open: gt, lt
  or or_14 (AC_LOAD, DR, ADD_OUTPUT, AND_OUTPUT, rB9, rB7, rB6);
  or or_15 (CLEAR_SC, AND_OUTPUT, ADD_OUTPUT, DR, STA, BUN, BSA, ISZ, r);
  Comparator #(.width(16)) comparator_2 (.a(in_2), .b(DR_DATA), .eq(DR_EQUAL_0));  // open: gt, lt

  // Other names for the same wires on the sheet: AC_LAST_BIT = AC_DATA[15]; DR_LAST_BIT = DR_DATA[15]; PC_CLEAR = RST

  // Notes on the sheet:
  //   AR_CONTROL_LOGIC
  //   Memory_read_enable
  //   CPU_START
  //   Bharat Processor
  //   PC_CONTROL_LOGIC
  //   Here Temopary Register is not used
  //   X6 remains un used
  //   Memory_write_enable
  //   CLEAR_SEQUENCE COUNTER
  //   AC_CONTROL_LOGIC
endmodule

module Data_Path (
  input  Write_en_memory,
  input  Read_en_memory,
  input  CLOCK,
  input  AR_INR,
  input  AR_CLR,
  input  AR_LD,
  input  PC_INR,
  input  PC_CLR,
  input  PC_LD,
  input  [2:0] S2S1S0,
  input  DR_INR,
  input  DR_CLR,
  input  DR_LD,
  input  AC_INR,
  input  AC_CLR,
  input  AC_LD,
  input  IR_LD,
  input  TR_INR,
  input  TR_CLR,
  input  TR_LD,
  input  [2:0] ALU_SELECT,
  input  compE,
  input  D1T5,
  input  Eclear,
  input  rB7,
  input  Eload,
  input  rB6,
  output [15:0] DR_DATA,
  output [15:0] AC_DATA,
  output [15:0] IR_DATA
);

  wire Cout, ExtraFF_output;
  wire [11:0] AR_addresspin;
  wire [15:0] ALU_OUT, AR_data_out, multiplexer_1_out, PC_data_out, ram_1_dout, TR_data_out;

  RAM #(.addrWidth(12), .asyncread("true"), .dataWidth(16)) ram_1 (
    .addr(AR_addresspin), .we(Write_en_memory), .oe(Read_en_memory), .clk(CLOCK), .din(multiplexer_1_out),
    .dout(ram_1_dout));
  // Probe on AR_addresspin
  addressRegister AR (
    .INR(AR_INR), .CLEAR(AR_CLR), .CLOCK(CLOCK), .LOAD(AR_LD), .DATA_IN(multiplexer_1_out),
    .AddressPin(AR_addresspin), .DATA_OUT(AR_data_out));
  programCounterReg PC (
    .INR(PC_INR), .CLEAR(PC_CLR), .CLOCK(CLOCK), .LOAD(PC_LD), .DATA_IN(multiplexer_1_out),
    .DATA_OUT(PC_data_out));
  commonRegAcDrTr DR (
    .INR(DR_INR), .CLEAR(DR_CLR), .CLOCK(CLOCK), .DATA_IN(multiplexer_1_out), .LOAD(DR_LD), .DATA_OUT(DR_DATA));
  commonRegAcDrTr AC (.INR(AC_INR), .CLEAR(AC_CLR), .CLOCK(CLOCK), .DATA_IN(ALU_OUT), .LOAD(AC_LD), .DATA_OUT(AC_DATA));
  instructionRegister IR (.DATA_IN(multiplexer_1_out), .LOAD(IR_LD), .CLOCK(CLOCK), .DATA_OUT(IR_DATA));
  commonRegAcDrTr TR (
    .INR(TR_INR), .CLEAR(TR_CLR), .CLOCK(CLOCK), .DATA_IN(multiplexer_1_out), .LOAD(TR_LD),
    .DATA_OUT(TR_data_out));
  ALU alu_1 (
    .AC(AC_DATA), .DR(DR_DATA), .ALUselect(ALU_SELECT), .shl(ExtraFF_output), .shr(ExtraFF_output),
    .Cout(Cout), .ALU_out(ALU_OUT));  // open: INPR
  ExtraFF extraff_1 (
    .C_OUT(Cout), .AC_0(AC_DATA[0]), .compE(AC_DATA[15]), .AC_15(compE), .D1T5(D1T5), .clr(Eclear),
    .rB7(rB7), .load(Eload), .clk(CLOCK), .rB6(rB6), .op(ExtraFF_output));
  // Probe on PC_data_out
  // Probe on AR_data_out
  // Probe on ram_1_dout
  Multiplexer #(.select(3), .width(16)) multiplexer_1 (
    .in1(AR_data_out), .in2(PC_data_out), .in3(DR_DATA), .in4(AC_DATA), .in5(IR_DATA), .in6(TR_data_out),
    .in7(ram_1_dout), .out(multiplexer_1_out), .sel(S2S1S0));  // open: in0

  // Other names for the same wires on the sheet: AC_0 = AC_DATA[0]; AC_15 = AC_DATA[15]
endmodule

module ALU (
  input  [15:0] AC,
  input  [15:0] DR,
  input  [15:0] INPR,
  input  [2:0] ALUselect,
  input  shl,
  input  shr,
  output Cout,
  output [15:0] ALU_out
);

  wire [15:0] adder_1_out, and_1_out, not_1_out;

  Adder #(.width(16)) adder_1 (.a(AC), .b(DR), .out(adder_1_out), .cin(1'b0), .cout(Cout));
  assign and_1_out = AC & DR;  // AND_Gate and_1, 16 bits wide
  assign not_1_out = ~AC;  // NOT_Gate not_1, 16 bits wide
  Multiplexer #(.select(3), .width(16)) multiplexer_1 (
    .in1(and_1_out), .in2(adder_1_out), .in3(DR), .in4(INPR), .in5(not_1_out), .in6({shr, AC[15:1]}),
    .in7({AC[14:0], shl}), .out(ALU_out), .sel(ALUselect));  // open: in0
endmodule

module ALU_SELECT_GENERATOR (
  input  a1,
  input  a3,
  input  a5,
  input  a7,
  input  a2,
  input  a6,
  input  a4,
  output [2:0] n2n1n0
);

  or or_1 (n2n1n0[0], a1, a3, a5, a7);
  or or_2 (n2n1n0[1], a7, a3, a2, a6);
  or or_3 (n2n1n0[2], a6, a5, a7, a4);

  // Notes on the sheet:
  //   n0
  //   n1
  //   n2
endmodule

module BUS_SELECT_GENERATOR (
  input  x1,
  input  x2,
  input  x3,
  input  x4,
  input  x5,
  input  x6,
  input  x7,
  output [2:0] o3o2o1
);

  wire [2:0] o1_out;

  or o1 (o1_out[0], x1, x3, x5, x7);
  or o2 (o1_out[1], x2, x3, x6, x7);
  or o3 (o1_out[2], x4, x5, x6, x7);
  Priority_Encoder priority_encoder_1 (
    .in1(x1), .in2(x2), .in3(x3), .in4(x4), .in5(x5), .in6(x6), .in7(x7), .out(o3o2o1));  // open: in0, en_in, gs, en_out
endmodule

module ExtraFF (
  input  C_OUT,
  input  AC_0,
  input  compE,
  input  AC_15,
  input  D1T5,
  input  clr,
  input  rB7,
  input  load,
  input  clk,
  input  rB6,
  output op
);

  wire and_1_out, and_2_out, and_3_out, E_INPUT, multiplexer_1_out, multiplexer_2_out, multiplexer_3_out,
       not_1_out;
  wire [1:0] or_1_out;

  not not_1 (not_1_out, op);
  Multiplexer multiplexer_1 (.in0(op), .in1(not_1_out), .out(multiplexer_1_out), .sel(compE));
  Multiplexer multiplexer_2 (.in0(multiplexer_1_out), .in1(E_INPUT), .out(multiplexer_2_out), .sel(load));
  Multiplexer multiplexer_3 (.in0(multiplexer_2_out), .in1(1'b0), .out(multiplexer_3_out), .sel(clr));
  D_Flip_Flop d_ff_1 (.D(multiplexer_3_out), .clk(clk), .Q(op));  // open: Qn, preset, reset
  and and_1 (and_1_out, D1T5, C_OUT);
  and and_2 (and_2_out, AC_0, rB7);
  or or_1 (or_1_out[0], D1T5, rB6);
  or or_2 (or_1_out[1], rB7, rB6);
  and and_3 (and_3_out, AC_15, rB6);
  Multiplexer #(.select(2)) multiplexer_4 (
    .in1(and_1_out), .in2(and_2_out), .in3(and_3_out), .out(E_INPUT), .sel(or_1_out));  // open: in0
endmodule
